# Fritzing sketch PiAudioLooper-AdaFruit-MAX98306 (saved by Fritzing 1.0.1rc)

parts:
  A1 = Raspberry Pi 3 Model A+
  S1 = Momentary Switch [package=ksa_sealed_tac_switch]
  LED1 = LED - 3mm [color="Red (633nm)" current=0.030 package="3 mm [THT]"]
  R1 = Resistor [tolerance=±5% power=0.25 resistance=330 package=THT]
  Part1 = Adafruit MAX98306 Stereo 3.7W Class D Audio Amplifier [part_number="Adafruit #987"]

nets:
  N1: A1.Pin_1, A1.Pin_16, A1.Pin_24, A1.Pin_26, A1.Pin_38, S1.2, R1.Pin_1, Part1.GND
  N2: A1.Pin_21, S1.4
  N3: A1.Pin_23, LED1.anode
  N4: A1.Pin_39, A1.Pin_40, Part1.VDD
  N5: LED1.cathode, R1.Pin_0

custom parts:
  Raspberry Pi 3 Model A+: The Raspberry Pi 3 Model A+ is the latest product in the Raspberry Pi 3 range. Like the Raspberry Pi 3 Model B+, it boasts a 64-bit quad core processor running at 1.4 GHz, dual-band 2.4 GHz and 5 GHz wireless LAN, and Bluetooth 4.2/BLE.
  Adafruit MAX98306 Stereo 3.7W Class D Audio Amplifier: This incredibly small stereo amplifier is surprisingly powerful - able to deliver 2 x 3.7W channels into 3 ohm impedance speakers. Inside the miniature chip is a class D controller, able to run from 2.7V-5.5VDC. Since the amp is a class D, its incredibly efficient (over 90% efficient when driving an 8Ω speaker at over a Watt) - making it perfect for portable and battery-powered projects. It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
